// Logisim project 2-BIT MAGNATEIC- COMPARATOR.circ as structural Verilog: 1 circuit, main circuit main
module main (
  input  a,
  input  b,
  input  c,
  input  d,
  output x,
  output y,
  output z
);

  wire and_1_out, and_2_out, and_3_out, and_4_out, and_5_out, and_6_out, and_7_out, and_8_out, and_9_out,
       and_10_out, not_1_out, not_2_out, not_3_out, not_4_out, not_5_out, not_6_out, not_7_out, not_8_out,
       not_9_out, not_10_out, not_11_out, not_12_out, not_13_out, not_14_out, not_15_out, not_16_out;

  not not_1 (not_1_out, a);
  and and_1 (and_1_out, not_1_out, not_2_out, d);
  not not_2 (not_2_out, b);
  not not_3 (not_3_out, a);
  and and_2 (and_2_out, not_3_out, c);
  not not_4 (not_4_out, b);
  and and_3 (and_3_out, not_4_out, c, d);
  not not_5 (not_5_out, a);
  not not_6 (not_6_out, b);
  not not_7 (not_7_out, c);
  not not_8 (not_8_out, d);
  not not_9 (not_9_out, a);
  not not_10 (not_10_out, c);
  not not_11 (not_11_out, b);
  not not_12 (not_12_out, d);
  and and_4 (and_4_out, b, not_13_out, not_14_out);
  not not_13 (not_13_out, c);
  not not_14 (not_14_out, d);
  and and_5 (and_5_out, a, not_15_out);
  not not_15 (not_15_out, c);
  and and_6 (and_6_out, a, b, not_16_out);
  not not_16 (not_16_out, d);
  or or_1 (x, and_1_out, and_2_out, and_3_out);
  and and_7 (and_7_out, not_5_out, not_6_out, not_7_out, not_8_out);
  and and_8 (and_8_out, not_9_out, b, not_10_out, d);
  and and_9 (and_9_out, a, not_11_out, c, not_12_out);
  and and_10 (and_10_out, a, b, c, d);
  or or_2 (z, and_4_out, and_5_out, and_6_out);
  or or_3 (y, and_7_out, and_8_out, and_9_out, and_10_out);
endmodule
