// Logisim project Smart Parking System.circ as structural Verilog: 1 circuit, main circuit main
module main (
  input  in_1,
  input  in_2,
  input  in_3,
  input  in_4,
  output SLOT_1,
  output SLOT_2,
  output SLOT_3,
  output SLOT_4,
  output LOT_FULL,
  output SPACE_AVAIL
);

  and and_1 (LOT_FULL, in_1, in_2, in_3, in_4);
  not not_1 (SPACE_AVAIL, LOT_FULL);

  assign SLOT_1 = in_1;
  assign SLOT_2 = in_2;
  assign SLOT_3 = in_3;
  assign SLOT_4 = in_4;
endmodule
